// Logisim project thedonger.circ as structural Verilog: 1 circuit, main circuit main
module main (
);

  wire CPUClock_out, DataClock_out, decoder_1_out0, decoder_1_out1, decoder_1_out2, decoder_1_out3;
  wire [7:0] adder_1_out, adder_2_out, multiplexer_1_out, multiplexer_2_out, multiplexer_3_out,
       multiplexer_4_out, multiplexer_5_out, PC_q, ram_2_dout, subtractor_1_out, X0_q, X1_q, X2_q, X3_q;
  wire [15:0] ram_1_dout;

  Adder adder_1 (.a(PC_q), .b(8'h1), .out(adder_1_out));  // open: cin, cout
  Clock #(.highDuration(2), .lowDuration(2)) CPUClock (.out(CPUClock_out));
  Register PC (.D(adder_1_out), .clk(CPUClock_out), .Q(PC_q));  // open: en, clr
  RAM #(.dataWidth(16), .enables("line")) ram_1 (
    .addr(PC_q), .we(1'b0), .clk(CPUClock_out), .dout(ram_1_dout));  // open: din
  Decoder #(.select(2)) decoder_1 (
    .out0(decoder_1_out0), .out1(decoder_1_out1), .out2(decoder_1_out2), .out3(decoder_1_out3),
    .sel(ram_1_dout[8:7]));  // open: en
  Register X0 (.D(multiplexer_5_out), .en(decoder_1_out0), .clk(CPUClock_out), .Q(X0_q));  // open: clr
  Register X1 (.D(multiplexer_5_out), .en(decoder_1_out1), .clk(CPUClock_out), .Q(X1_q));  // open: clr
  Register X2 (.D(multiplexer_5_out), .en(decoder_1_out2), .clk(CPUClock_out), .Q(X2_q));  // open: clr
  Register X3 (.D(multiplexer_5_out), .en(decoder_1_out3), .clk(CPUClock_out), .Q(X3_q));  // open: clr
  Hex_Digit_Display X0Val (.value(X0_q[7:4]));  // open: dp
  Hex_Digit_Display X1Val (.value(X1_q[7:4]));  // open: dp
  Hex_Digit_Display X2Val (.value(X2_q[7:4]));  // open: dp
  Hex_Digit_Display X3Val (.value(X3_q[7:4]));  // open: dp
  Hex_Digit_Display hex_digit_display_1 (.value(X0_q[3:0]));  // open: dp
  Multiplexer #(.select(2), .width(8)) multiplexer_1 (
    .in0(X0_q), .in1(X1_q), .in2(X2_q), .in3(X3_q), .out(multiplexer_1_out), .sel(ram_1_dout[4:3]));
  Hex_Digit_Display hex_digit_display_2 (.value(X1_q[3:0]));  // open: dp
  Hex_Digit_Display hex_digit_display_3 (.value(X2_q[3:0]));  // open: dp
  Multiplexer #(.select(2), .width(8)) multiplexer_2 (
    .in0(X0_q), .in1(X1_q), .in2(X2_q), .in3(X3_q), .out(multiplexer_2_out), .sel(ram_1_dout[6:5]));
  Hex_Digit_Display hex_digit_display_4 (.value(X3_q[3:0]));  // open: dp
  Multiplexer #(.width(8)) multiplexer_3 (
    .in0(multiplexer_2_out), .in1({2'b00, ram_1_dout[14:9]}), .out(multiplexer_3_out), .sel(ram_1_dout[0]));
  Adder adder_2 (.a(multiplexer_1_out), .b(multiplexer_3_out), .out(adder_2_out));  // open: cin, cout
  Subtractor subtractor_1 (.a(multiplexer_1_out), .b(multiplexer_3_out), .out(subtractor_1_out));  // open: bin, bout
  Multiplexer #(.width(8)) multiplexer_4 (
    .in0(subtractor_1_out), .in1(adder_2_out), .out(multiplexer_4_out), .sel(ram_1_dout[2]));
  Clock DataClock (.out(DataClock_out));
  RAM #(.enables("line")) ram_2 (
    .addr(multiplexer_4_out), .we(1'b0), .clk(DataClock_out), .dout(ram_2_dout));  // open: din
  Multiplexer #(.width(8)) multiplexer_5 (
    .in0(multiplexer_4_out), .in1(ram_2_dout), .out(multiplexer_5_out), .sel(ram_1_dout[1]));

  // Notes on the sheet:
  //   Alexander Ha and Christopher Arias
  //   I pledge my honor that I have abided by the Stevens Honor System
  //   Instruction Memory
  //   InstructionRAM
  //   Register File
  //   RegData2
  //   RegData1
  //   RegisterOrImmediateMultiplexor
  //   ValueData2
  //   Adder
  //   ALU
  //   Subber
  //   AddSignal
  //   RegDataW
  //   AddOrSubMultiplexor
  //   DataRAM
  //   Data Memory
  //   ldrSignal
  //   RegDataWMultiplexor
endmodule
